# Fritzing sketch controller (saved by Fritzing 0.9.6b)

parts:
  Part12 = Adafruit FeatherWing Proto [part_number="Adafruit #2884"]

nets:
  N1: Part12.N, Part12.N$36, Part12.N$37
  N2: Part12.M, Part12.N$43, Part12.N$48
  N3: Part12.L, Part12.N$49, Part12.N$50
  N4: Part12.K, Part12.N$94, Part12.N$113
  N5: Part12.I, Part12.N$105, Part12.N$114, Part12.N$118
  N6: Part12.H, Part12.N$111, Part12.N$119, Part12.N$121
  N7: Part12.SCL, Part12.N$116, Part12.N$130, Part12.N$133
  N8: Part12.SDA, Part12.N$123, Part12.N$125, Part12.N$129
  N9: Part12.3V, Part12.N$92, Part12.N$93
  N10: Part12.GND, Part12.N$52, Part12.N$53, Part12.N$79

notes:
  solder
  wire

custom parts:
  Adafruit FeatherWing Proto: This is the FeatherWing Proto - a prototyping add-on for all Feather boards. Using our Feather Stacking Headers or Feather Female Headers you can connect a FeatherWing on top or bottom of your Feather board and let the board take flight! This has a duplicate breakout for each pin on a Feather, as well as a bunch of plain grid proto holes. For GND and 3.3V, we give you a strip of connected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

// code stored in the sketch: controller.ino

