# Fritzing sketch new controller (saved by Fritzing 0.9.6b)

parts:
  Part1 = Adafruit FeatherWing Proto [part_number="Adafruit #2884"]
  S2 = Momentary Switch [package=ksa_sealed_tac_switch]
  S1 = Pushbutton [package="[THT]"]  # not connected
  S3 = Momentary Switch [package=ksa_sealed_tac_switch]
  R1 = Resistor [tolerance=±5% power=0.25 resistance=220 package=THT]

nets:
  N1: Part1.M, Part1.N$91
  N2: Part1.L, Part1.N$106
  N3: Part1.K, Part1.N$89
  N4: Part1.GND, R1.Pin_1
  N5: Part1.3V, Part1.N$66, Part1.N$108
  N6: Part1.N$46, R1.Pin_0
  N7: Part1.N$47, Part1.N$73
  N8: Part1.N$48, Part1.N$121
  N9: Part1.N$75, S2.4
  N10: Part1.N$77, S2.2
  N11: Part1.N$90, S2.3
  N12: Part1.N$92, S2.1
  N13: Part1.N$99, Part1.N$123
  N14: Part1.N$105, S3.2
  N15: Part1.N$107, S3.4
  N16: Part1.N$120, S3.1
  N17: Part1.N$122, S3.3

custom parts:
  Adafruit FeatherWing Proto: This is the FeatherWing Proto - a prototyping add-on for all Feather boards. Using our Feather Stacking Headers or Feather Female Headers you can connect a FeatherWing on top or bottom of your Feather board and let the board take flight! This has a duplicate breakout for each pin on a Feather, as well as a bunch of plain grid proto holes. For GND and 3.3V, we give you a strip of connected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
